// Logisim project minirv_CPU.circ as structural Verilog: 12 circuits, main circuit main
module main (
  input  in_1,
  input  in_2
);

  wire and_1_out, and_2_out, clock_1_out, decoder_io_1_ismem, decoder_io_1_isvga, or_1_out, or_2_out;
  wire [1:0] encoder_42_1_y, multiplexer_6_out;
  wire [2:0] encoder_83_1_y;
  wire [3:0] decode_i_1_rd, decode_i_1_rs1, decode_j_1_rd, decode_j_1_rs1, decode_l_1_rd, decode_l_1_rs1,
       decode_l_2_rd, decode_l_2_rs1, decode_r_1_rd, decode_r_1_rs1, decode_r_1_rs2, decode_s_1_rs1,
       decode_s_1_rs2, decode_s_2_rs1, decode_s_2_rs2, decode_u_1_rd, decoder_1_out3, multiplexer_2_out,
       multiplexer_3_out, multiplexer_5_out, multiplexer_7_out;
  wire [7:0] decode_cmd_1_cmd_type, gpr_1_rdata2_2, multiplexer_1_out;
  wire [23:0] multiplexer_6_out_2, rgb_video_1_p6;
  wire [31:0] adder_1_out, adder_2_out, adder_3_out, adder_4_out, adder_5_out, adder_6_out, adder_7_out,
       adder_8_out, bit_extender_1_out, decode_cmd_1_add, decode_cmd_1_addi, decode_cmd_1_jalr,
       decode_cmd_1_lbu, decode_cmd_1_lui, decode_cmd_1_lw, decode_cmd_1_sb, decode_cmd_1_sw, decode_i_1_imm,
       decode_j_1_imm, decode_l_1_imm, decode_l_2_imm, decode_s_1_imm, decode_s_2_imm, decode_u_1_imm,
       gpr_1_rdata1, multiplexer_4_out, multiplexer_8_out, multiplexer_9_out, PC_q, ram_1_dout, rom_1_data;
  wire [31:8] gpr_1_rdata2;
  wire [31:26] multiplexer_6_out_3;

  Clock clock_1 (.out(clock_1_out));
  Register #(.width(32)) PC (.D(multiplexer_9_out), .en(in_1), .clk(clock_1_out), .Q(PC_q));  // open: clr
  ROM #(.addrWidth(24), .dataWidth(32)) rom_1 (.addr(PC_q[25:2]), .data(rom_1_data));
  decode_cmd decode_cmd_1 (
    .cmd(rom_1_data), .addi(decode_cmd_1_addi), .jalr(decode_cmd_1_jalr), .add(decode_cmd_1_add),
    .lui(decode_cmd_1_lui), .lw(decode_cmd_1_lw), .lbu(decode_cmd_1_lbu), .sw(decode_cmd_1_sw),
    .sb(decode_cmd_1_sb), .cmd_type(decode_cmd_1_cmd_type));
  or or_1 (or_1_out, decode_cmd_1_cmd_type[0], decode_cmd_1_cmd_type[1], decode_cmd_1_cmd_type[2], decode_cmd_1_cmd_type[3], decode_cmd_1_cmd_type[4], decode_cmd_1_cmd_type[5]);
  or or_2 (or_2_out, decode_cmd_1_cmd_type[6], decode_cmd_1_cmd_type[7]);
  decode_I decode_i_1 (.cmd(decode_cmd_1_addi), .rd(decode_i_1_rd), .rs1(decode_i_1_rs1), .imm(decode_i_1_imm));
  decode_J decode_j_1 (.cmd(decode_cmd_1_jalr), .rd(decode_j_1_rd), .rs1(decode_j_1_rs1), .imm(decode_j_1_imm));
  decode_R decode_r_1 (.cmd(decode_cmd_1_add), .rd(decode_r_1_rd), .rs1(decode_r_1_rs1), .rs2(decode_r_1_rs2));
  decode_U decode_u_1 (.cmd(decode_cmd_1_lui), .rd(decode_u_1_rd), .imm(decode_u_1_imm));
  decode_L decode_l_1 (.cmd(decode_cmd_1_lw), .rd(decode_l_1_rd), .rs1(decode_l_1_rs1), .imm(decode_l_1_imm));
  decode_L decode_l_2 (.cmd(decode_cmd_1_lbu), .rd(decode_l_2_rd), .rs1(decode_l_2_rs1), .imm(decode_l_2_imm));
  decode_S decode_s_1 (.cmd(decode_cmd_1_sw), .rs1(decode_s_1_rs1), .rs2(decode_s_1_rs2), .imm(decode_s_1_imm));
  decode_S decode_s_2 (.cmd(decode_cmd_1_sb), .rs1(decode_s_2_rs1), .rs2(decode_s_2_rs2), .imm(decode_s_2_imm));
  Adder #(.width(32)) adder_1 (.a(decode_i_1_imm), .b(gpr_1_rdata1), .out(adder_1_out));  // open: cin, cout
  Adder #(.width(32)) adder_2 (.a(decode_j_1_imm), .b(gpr_1_rdata1), .out(adder_2_out));  // open: cin, cout
  Adder #(.width(32)) adder_3 (
    .a(gpr_1_rdata1), .b({gpr_1_rdata2, gpr_1_rdata2_2}), .out(adder_3_out));  // open: cin, cout
  Adder #(.width(32)) adder_4 (.a(decode_l_1_imm), .b(gpr_1_rdata1), .out(adder_4_out));  // open: cin, cout
  Adder #(.width(32)) adder_5 (.a(decode_l_2_imm), .b(gpr_1_rdata1), .out(adder_5_out));  // open: cin, cout
  Adder #(.width(32)) adder_6 (.a(decode_s_1_imm), .b(gpr_1_rdata1), .out(adder_6_out));  // open: cin, cout
  Adder #(.width(32)) adder_7 (.a(decode_s_2_imm), .b(gpr_1_rdata1), .out(adder_7_out));  // open: cin, cout
  encoder_42 encoder_42_1 (
    .A0(decode_cmd_1_cmd_type[4]), .A1(decode_cmd_1_cmd_type[5]), .A2(decode_cmd_1_cmd_type[6]),
    .A3(decode_cmd_1_cmd_type[7]), .Y(encoder_42_1_y));
  encoder_83 encoder_83_1 (
    .A0(decode_cmd_1_cmd_type[0]), .A1(decode_cmd_1_cmd_type[1]), .A2(decode_cmd_1_cmd_type[2]),
    .A3(decode_cmd_1_cmd_type[3]), .A4(decode_cmd_1_cmd_type[4]), .A5(decode_cmd_1_cmd_type[5]),
    .A6(decode_cmd_1_cmd_type[6]), .A7(decode_cmd_1_cmd_type[7]), .Y(encoder_83_1_y));
  Multiplexer #(.select(2), .width(8)) multiplexer_1 (
    .in0(ram_1_dout[7:0]), .in1(ram_1_dout[15:8]), .in2(ram_1_dout[23:16]), .in3(ram_1_dout[31:24]),
    .out(multiplexer_1_out), .sel(multiplexer_6_out));
  Multiplexer #(.select(3), .width(4)) multiplexer_2 (
    .in2(decode_r_1_rs2), .in6(decode_s_1_rs2), .in7(decode_s_2_rs2), .out(multiplexer_2_out),
    .sel(encoder_83_1_y));  // open: in0, in1, in3, in4, in5
  assign bit_extender_1_out = {{24{1'b0}}, multiplexer_1_out};  // Bit_Extender bit_extender_1
  Multiplexer #(.select(3), .width(4)) multiplexer_3 (
    .in0(decode_i_1_rd), .in1(decode_j_1_rd), .in2(decode_r_1_rd), .in3(decode_u_1_rd), .in4(decode_l_1_rd),
    .in5(decode_l_2_rd), .out(multiplexer_3_out), .sel(encoder_83_1_y));  // open: in6, in7
  Multiplexer #(.select(3), .width(32)) multiplexer_4 (
    .in0(adder_1_out), .in1(adder_8_out), .in2(adder_3_out), .in3(decode_u_1_imm), .in4(ram_1_dout),
    .in5(bit_extender_1_out), .out(multiplexer_4_out), .sel(encoder_83_1_y));  // open: in6, in7
  Multiplexer #(.select(3), .width(4)) multiplexer_5 (
    .in0(decode_i_1_rs1), .in1(decode_j_1_rs1), .in2(decode_r_1_rs1), .in4(decode_l_1_rs1),
    .in5(decode_l_2_rs1), .in6(decode_s_1_rs1), .in7(decode_s_2_rs1), .out(multiplexer_5_out),
    .sel(encoder_83_1_y));  // open: in3
  GPR gpr_1 (
    .clk(clock_1_out), .waddr(multiplexer_3_out), .wdata(multiplexer_4_out), .wen(or_1_out),
    .raddr1(multiplexer_5_out), .raddr2(multiplexer_2_out), .rdata1(gpr_1_rdata1),
    .rdata2({gpr_1_rdata2, gpr_1_rdata2_2}));
  Multiplexer #(.select(2), .width(32)) multiplexer_6 (
    .in0(adder_4_out), .in1(adder_5_out), .in2(adder_6_out), .in3(adder_7_out),
    .out({multiplexer_6_out_3, multiplexer_6_out_2, multiplexer_6_out}), .sel(encoder_42_1_y));
  Decoder #(.select(2)) decoder_1 (
    .out0(decoder_1_out3[3]), .out1(decoder_1_out3[2]), .out2(decoder_1_out3[1]), .out3(decoder_1_out3[0]),
    .sel(multiplexer_6_out), .en(1'b1));
  Multiplexer #(.width(4)) multiplexer_7 (
    .in0(4'b1111), .in1(decoder_1_out3), .out(multiplexer_7_out), .sel(decode_cmd_1_cmd_type[7]));
  Multiplexer #(.width(32)) multiplexer_8 (
    .in0({gpr_1_rdata2, gpr_1_rdata2_2}),
    .in1({gpr_1_rdata2_2, gpr_1_rdata2_2, gpr_1_rdata2_2, gpr_1_rdata2_2}), .out(multiplexer_8_out),
    .sel(decode_cmd_1_cmd_type[7]));
  decoder_IO decoder_io_1 (
    .in_1({multiplexer_6_out_3, multiplexer_6_out_2, multiplexer_6_out}), .isVGA(decoder_io_1_isvga),
    .isMem(decoder_io_1_ismem));
  and and_1 (and_1_out, or_2_out, decoder_io_1_ismem);
  RAM #(.addrWidth(24), .asyncread("true"), .byteenables("byteEnables"), .dataWidth(32), .\type ("nonvolatile")) ram_1 (
    .addr(multiplexer_6_out_2), .we(and_1_out), .oe(1'b1), .clk(clock_1_out), .din(multiplexer_8_out),
    .dout(ram_1_dout), .be3(multiplexer_7_out[0]), .be2(multiplexer_7_out[1]), .be1(multiplexer_7_out[2]),
    .be0(multiplexer_7_out[3]));
  and and_2 (and_2_out, decoder_io_1_isvga, decode_cmd_1_cmd_type[6]);
  Adder #(.width(32)) adder_8 (.a(PC_q), .b(32'h4), .out(adder_8_out));  // open: cin, cout
  Multiplexer #(.width(32)) multiplexer_9 (
    .in0(adder_8_out), .in1(adder_2_out), .out(multiplexer_9_out), .sel(decode_cmd_1_cmd_type[1]));
  // RGB_Video #(.cursor("No Cursor"), .height(256), .width(256)) rgb_video_1: pin names not known; wires that end beside it: in_2, clock_1_out, and_2_out, multiplexer_6_out_2[7:0], multiplexer_6_out_2[15:8], rgb_video_1_p6
  Bit_Extender #(.in_width(32), .out_width(24), .\type ("zero")) bit_extender_2 (
    .in(multiplexer_8_out), .out(rgb_video_1_p6));

  // Notes on the sheet:
  //   contents of rom_1 (hex, n*v repeats v):
  //   413 93137 10113 10b7 dbc08093 80e7 fe012823 fea10923 fea12423 fe914203 fe4109a3 ff012783 f787b3
  //   f787b3 4b6b7 af868693 fdc10113 d787b3 10000713 f12423 10593 100793 b00513 2112023 12023 12223 e12623
  //   e12823 f10a23 10b7 a8408093 80e7 2012083 2410113 8067 ff410113 112423 10b7 a7c08093 80e7 513 1800093
  //   80e7 812083 513 c10113 8067 852583 feb12823 fe812e23 3437 80840413 ff014183 3401b3 1c183 ff114203
  //   440233 24203 4181b3 ff214203 440233 24203 4181b3 ff314203 440233 24203 4181b3 3237 80020213 320233
  //   24203 ffc12403 420233 420233 410233 11b7 86418193 fe312823 14800193 fe312623 fec22203 20067 1052703
  //   52683 452783 fe810113 e12423 112a23 812823 912623 fed12823 fef12623 13737 a0070713 fe012223 ff314203
  //   fe4102a3 fef14203 fe410223 fe412203 470233 24203 fe4105a3 ff214203 fe4102a3 fee14203 fe410223
  //   fe412203 470233 24203 fe410523 ff114203 fe4102a3 fed14203 fe410223 fe412203 470233 24203 fe4104a3
  //   ff014203 fe4102a3 fec14203 fe410223 fe412203 470233 24203 fe410423 fe812703 c52603 fee12823 fe812e23
  //   3437 80840413 ff014183 3401b3 1c183 ff114203 440233 24203 4181b3 ff214203 440233 24203 4181b3
  //   ff314203 440233 24203 4181b3 3237 80020213 320233 24203 ffc12403 420233 420233 410233 66800193
  //   fe312823 28800193 fe312623 fec22203 20067 c68733 10000513 fe812e23 fe912c23 fee12823 50413 ff012483
  //   fe812423 feb14183 3181b3 fe312423 fe914183 3181b3 fe912423 feb14203 420233 fe412423 fe914203 4181b3
  //   3181b3 fe312a23 fe912423 33237 90020213 feb14183 4181b3 1c183 fe3103a3 fea14183 4181b3 1c183
  //   fe310323 fe914183 4181b3 1c183 fe3102a3 fe814183 4181b3 1c183 fe310223 ff412183 fe412203 440233
  //   120213 fe412423 feb14203 420233 fe412423 fe914203 4181b3 3237 90820213 320233 ff812483 ffc12403
  //   24203 420233 420233 410233 11b7 86818193 fe312823 39000193 fe312623 fec22203 20067 812703 10000513
  //   e78733 fe812e23 fe912c23 fee12823 50413 ff012483 fe812423 feb14183 3181b3 fe312423 fe914183 3181b3
  //   fe912423 feb14203 420233 fe412423 fe914203 4181b3 3181b3 fe312a23 fe912423 33237 90020213 feb14183
  //   4181b3 1c183 fe3103a3 fea14183 4181b3 1c183 fe310323 fe914183 4181b3 1c183 fe3102a3 fe814183 4181b3
  //   1c183 fe310223 ff412183 fe412203 440233 120213 fe412423 feb14203 420233 fe412423 fe914203 4181b3
  //   3237 90820213 320233 ff812483 ffc12403 24203 420233 420233 410233 11b7 86818193 fe312823 49c00193
  //   fe312623 fec22203 20067 8*f787b3 d787b3 f787b3 f787b3 20000437 f40433 812783 c60633 c60633 fef12423
  //   feb14183 3181b3 fe312423 fe914183 fff78213 fe412423 feb14203 420233 fe412423 fe914203 4181b3 3237
  //   91820213 418233 24203 420233 420233 410233 65400193 fe312823 54000193 fe312623 fec22203 20067 493
  //   40513 b12223 c12023 10b7 de008093 80e7 12603 412583 812783 148493 40040413 c585b3 fef12823 fe912623
  //   fe812e23 fe912c23 2437 70040413 ff014183 340233 100193 320023 fec14183 3401b3 18023 24183 ff114483
  //   940233 100493 920023 fed14483 9404b3 48023 24483 9181b3 ff214483 940233 100493 920023 fee14483
  //   9404b3 48023 24483 9181b3 ff314483 940233 100493 920023 fef14483 9404b3 48023 24483 9181b3 3237
  //   80020213 320233 24203 ff812483 ffc12403 420233 420233 410233 65400193 fe312823 54400193 fe312623
  //   fec22203 20067 1412083 1012403 c12483 1810113 8067 10000713 fec12823 fee12623 fe812e23 fe912c23 2437
  //   70040413 ff014183 340233 100193 320023 fec14183 3401b3 18023 24183 ff114483 940233 100493 920023
  //   fed14483 9404b3 48023 24483 9181b3 ff214483 940233 100493 920023 fee14483 9404b3 48023 24483 9181b3
  //   ff314483 940233 100493 920023 fef14483 9404b3 48023 24483 9181b3 3237 80020213 320233 24203 ff812483
  //   ffc12403 420233 420233 410233 74c00193 fe312823 28800193 fe312623 fec22203 20067 812703 fee12823
  //   fec12623 fe812e23 fe912c23 2437 70040413 ff014183 340233 100193 320023 fec14183 3401b3 18023 24183
  //   ff114483 940233 100493 920023 fed14483 9404b3 48023 24483 9181b3 ff214483 940233 100493 920023
  //   fee14483 9404b3 48023 24483 9181b3 ff314483 940233 100493 920023 fef14483 9404b3 48023 24483 9181b3
  //   3237 80020213 320233 24203 ff812483 ffc12403 420233 420233 410233 11b7 83418193 fe312823 39000193
  //   fe312623 fec22203 20067 1012403 1412083 c12483 40637 20000537 1810113 1237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
endmodule

module GPR (
  input  clk,
  input  [3:0] waddr,
  input  [31:0] wdata,
  input  wen,
  input  [3:0] raddr1,
  input  [3:0] raddr2,
  output [31:0] rdata1,
  output [31:0] rdata2
);

  wire decoder_1_out1, decoder_1_out2, decoder_1_out3, decoder_1_out4, decoder_1_out5, decoder_1_out6,
       decoder_1_out7, decoder_1_out8, decoder_1_out9, decoder_1_out10, decoder_1_out11, decoder_1_out12,
       decoder_1_out13, decoder_1_out14, decoder_1_out15;
  wire [31:0] register_1_q, register_2_q, register_3_q, register_4_q, register_5_q, register_6_q,
       register_7_q, register_8_q, register_9_q, register_10_q, register_11_q, register_12_q, register_13_q,
       register_14_q, register_15_q, register_16_q;

  Decoder #(.select(4)) decoder_1 (
    .out1(decoder_1_out1), .out2(decoder_1_out2), .out3(decoder_1_out3), .out4(decoder_1_out4),
    .out5(decoder_1_out5), .out6(decoder_1_out6), .out7(decoder_1_out7), .out8(decoder_1_out8),
    .out9(decoder_1_out9), .out10(decoder_1_out10), .out11(decoder_1_out11), .out12(decoder_1_out12),
    .out13(decoder_1_out13), .out14(decoder_1_out14), .out15(decoder_1_out15), .sel(waddr), .en(wen));  // open: out0
  Register #(.width(32)) register_1 (.D(wdata), .en(1'b0), .clk(clk), .Q(register_1_q));  // open: clr
  Register #(.width(32)) register_2 (.D(wdata), .en(decoder_1_out8), .clk(clk), .Q(register_2_q));  // open: clr
  Register #(.width(32)) register_3 (.D(wdata), .en(decoder_1_out1), .clk(clk), .Q(register_3_q));  // open: clr
  Register #(.width(32)) register_4 (.D(wdata), .en(decoder_1_out9), .clk(clk), .Q(register_4_q));  // open: clr
  Register #(.width(32)) register_5 (.D(wdata), .en(decoder_1_out2), .clk(clk), .Q(register_5_q));  // open: clr
  Register #(.width(32)) register_6 (.D(wdata), .en(decoder_1_out10), .clk(clk), .Q(register_6_q));  // open: clr
  Register #(.width(32)) register_7 (.D(wdata), .en(decoder_1_out3), .clk(clk), .Q(register_7_q));  // open: clr
  Register #(.width(32)) register_8 (.D(wdata), .en(decoder_1_out11), .clk(clk), .Q(register_8_q));  // open: clr
  Register #(.width(32)) register_9 (.D(wdata), .en(decoder_1_out4), .clk(clk), .Q(register_9_q));  // open: clr
  Register #(.width(32)) register_10 (.D(wdata), .en(decoder_1_out12), .clk(clk), .Q(register_10_q));  // open: clr
  Register #(.width(32)) register_11 (.D(wdata), .en(decoder_1_out5), .clk(clk), .Q(register_11_q));  // open: clr
  Register #(.width(32)) register_12 (.D(wdata), .en(decoder_1_out13), .clk(clk), .Q(register_12_q));  // open: clr
  Register #(.width(32)) register_13 (.D(wdata), .en(decoder_1_out6), .clk(clk), .Q(register_13_q));  // open: clr
  Register #(.width(32)) register_14 (.D(wdata), .en(decoder_1_out14), .clk(clk), .Q(register_14_q));  // open: clr
  Register #(.width(32)) register_15 (.D(wdata), .en(decoder_1_out7), .clk(clk), .Q(register_15_q));  // open: clr
  Register #(.width(32)) register_16 (.D(wdata), .en(decoder_1_out15), .clk(clk), .Q(register_16_q));  // open: clr
  Multiplexer #(.select(4), .width(32)) multiplexer_1 (
    .in0(register_1_q), .in1(register_3_q), .in2(register_5_q), .in3(register_7_q), .in4(register_9_q),
    .in5(register_11_q), .in6(register_13_q), .in7(register_15_q), .in8(register_2_q), .in9(register_4_q),
    .in10(register_6_q), .in11(register_8_q), .in12(register_10_q), .in13(register_12_q),
    .in14(register_14_q), .in15(register_16_q), .out(rdata1), .sel(raddr1));
  Multiplexer #(.select(4), .width(32)) multiplexer_2 (
    .in0(register_1_q), .in1(register_3_q), .in2(register_5_q), .in3(register_7_q), .in4(register_9_q),
    .in5(register_11_q), .in6(register_13_q), .in7(register_15_q), .in8(register_2_q), .in9(register_4_q),
    .in10(register_6_q), .in11(register_8_q), .in12(register_10_q), .in13(register_12_q),
    .in14(register_14_q), .in15(register_16_q), .out(rdata2), .sel(raddr2));
endmodule

module decode_cmd (
  input  [31:0] cmd,
  output [31:0] addi,
  output [31:0] jalr,
  output [31:0] add,
  output [31:0] lui,
  output [31:0] lw,
  output [31:0] lbu,
  output [31:0] sw,
  output [31:0] sb,
  output [7:0] cmd_type
);

  wire comparator_1_eq, comparator_2_eq, comparator_3_eq, comparator_5_eq, comparator_6_eq, comparator_7_eq,
       comparator_8_eq, comparator_9_eq, comparator_10_eq, comparator_11_eq, comparator_12_eq,
       comparator_13_eq;
  wire [31:0] bit_extender_1_out, bit_extender_2_out, bit_extender_3_out, bit_extender_4_out,
       bit_extender_5_out, bit_extender_6_out, bit_extender_7_out, bit_extender_8_out;

  Comparator #(.width(7)) comparator_1 (.a(cmd[6:0]), .b(7'b0010011), .eq(comparator_1_eq));  // open: gt, lt
  Comparator #(.width(7)) comparator_2 (.a(cmd[6:0]), .b(7'b1100111), .eq(comparator_2_eq));  // open: gt, lt
  Comparator #(.width(7)) comparator_3 (.a(cmd[6:0]), .b(7'b0110011), .eq(comparator_3_eq));  // open: gt, lt
  Comparator #(.width(7)) comparator_4 (.a(cmd[6:0]), .b(7'b0110111), .eq(cmd_type[3]));  // open: gt, lt
  Comparator #(.width(7)) comparator_5 (.a(cmd[31:25]), .b({7{1'b0}}), .eq(comparator_5_eq));  // open: gt, lt
  Comparator #(.width(7)) comparator_6 (.a(cmd[6:0]), .b(7'b0000011), .eq(comparator_6_eq));  // open: gt, lt
  Comparator #(.width(3)) comparator_7 (.a(cmd[14:12]), .b(3'b010), .eq(comparator_7_eq));  // open: gt, lt
  Comparator #(.width(7)) comparator_8 (.a(cmd[6:0]), .b(7'b0000011), .eq(comparator_8_eq));  // open: gt, lt
  Comparator #(.width(3)) comparator_9 (.a(cmd[14:12]), .b(3'b100), .eq(comparator_9_eq));  // open: gt, lt
  Comparator #(.width(7)) comparator_10 (.a(cmd[6:0]), .b(7'b0100011), .eq(comparator_10_eq));  // open: gt, lt
  Comparator #(.width(3)) comparator_11 (.a(cmd[14:12]), .b(3'b010), .eq(comparator_11_eq));  // open: gt, lt
  Comparator #(.width(7)) comparator_12 (.a(cmd[6:0]), .b(7'b0100011), .eq(comparator_12_eq));  // open: gt, lt
  Comparator #(.width(3)) comparator_13 (.a(cmd[14:12]), .b(3'b000), .eq(comparator_13_eq));  // open: gt, lt
  and and_1 (cmd_type[0], comparator_1_eq, comparator_13_eq);
  and and_2 (cmd_type[1], comparator_2_eq, comparator_13_eq);
  and and_3 (cmd_type[2], comparator_3_eq, comparator_13_eq, comparator_5_eq);
  and and_4 (cmd_type[4], comparator_6_eq, comparator_7_eq);
  and and_5 (cmd_type[5], comparator_8_eq, comparator_9_eq);
  and and_6 (cmd_type[6], comparator_10_eq, comparator_11_eq);
  and and_7 (cmd_type[7], comparator_12_eq, comparator_13_eq);
  assign bit_extender_1_out = {{31{cmd_type[0]}}, cmd_type[0]};  // Bit_Extender bit_extender_1
  assign bit_extender_2_out = {{31{cmd_type[1]}}, cmd_type[1]};  // Bit_Extender bit_extender_2
  assign bit_extender_3_out = {{31{cmd_type[2]}}, cmd_type[2]};  // Bit_Extender bit_extender_3
  assign bit_extender_4_out = {{31{cmd_type[3]}}, cmd_type[3]};  // Bit_Extender bit_extender_4
  assign bit_extender_5_out = {{31{cmd_type[4]}}, cmd_type[4]};  // Bit_Extender bit_extender_5
  assign bit_extender_6_out = {{31{cmd_type[5]}}, cmd_type[5]};  // Bit_Extender bit_extender_6
  assign bit_extender_7_out = {{31{cmd_type[6]}}, cmd_type[6]};  // Bit_Extender bit_extender_7
  assign bit_extender_8_out = {{31{cmd_type[7]}}, cmd_type[7]};  // Bit_Extender bit_extender_8
  assign addi = cmd & bit_extender_1_out;  // AND_Gate and_8, 32 bits wide
  assign jalr = bit_extender_2_out & cmd;  // AND_Gate and_9, 32 bits wide
  assign add = bit_extender_3_out & cmd;  // AND_Gate and_10, 32 bits wide
  assign lui = bit_extender_4_out & cmd;  // AND_Gate and_11, 32 bits wide
  assign lw = bit_extender_5_out & cmd;  // AND_Gate and_12, 32 bits wide
  assign lbu = bit_extender_6_out & cmd;  // AND_Gate and_13, 32 bits wide
  assign sw = bit_extender_7_out & cmd;  // AND_Gate and_14, 32 bits wide
  assign sb = bit_extender_8_out & cmd;  // AND_Gate and_15, 32 bits wide

  // Notes on the sheet:
  //   opcode
  //   funct7
  //   funct3
endmodule

module decode_I (
  input  [31:0] cmd,
  output [3:0] rd,
  output [3:0] rs1,
  output [31:0] imm
);

  Bit_Extender #(.in_width(5), .out_width(4), .\type ("zero")) bit_extender_1 (.in(cmd[11:7]), .out(rd));
  Bit_Extender #(.in_width(5), .out_width(4), .\type ("zero")) bit_extender_2 (.in(cmd[19:15]), .out(rs1));
  assign imm = {{20{cmd[31]}}, cmd[31:20]};  // Bit_Extender bit_extender_3
endmodule

module decode_J (
  input  [31:0] cmd,
  output [3:0] rd,
  output [3:0] rs1,
  output [31:0] imm
);

  Bit_Extender #(.in_width(5), .out_width(4), .\type ("zero")) bit_extender_1 (.in(cmd[11:7]), .out(rd));
  Bit_Extender #(.in_width(5), .out_width(4), .\type ("zero")) bit_extender_2 (.in(cmd[19:15]), .out(rs1));
  assign imm = {{20{cmd[31]}}, cmd[31:20]};  // Bit_Extender bit_extender_3
endmodule

module decode_R (
  input  [31:0] cmd,
  output [3:0] rd,
  output [3:0] rs1,
  output [3:0] rs2
);

  Bit_Extender #(.in_width(5), .out_width(4), .\type ("zero")) bit_extender_1 (.in(cmd[11:7]), .out(rd));
  Bit_Extender #(.in_width(5), .out_width(4), .\type ("zero")) bit_extender_2 (.in(cmd[19:15]), .out(rs1));
  Bit_Extender #(.in_width(5), .out_width(4), .\type ("zero")) bit_extender_3 (.in(cmd[24:20]), .out(rs2));
endmodule

module decode_U (
  input  [31:0] cmd,
  output [3:0] rd,
  output [31:0] imm
);

  Bit_Extender #(.in_width(5), .out_width(4), .\type ("zero")) bit_extender_1 (.in(cmd[11:7]), .out(rd));

  assign imm = {cmd[31:12], {12{1'b0}}};
endmodule

module decode_L (
  input  [31:0] cmd,
  output [3:0] rd,
  output [3:0] rs1,
  output [31:0] imm
);

  Bit_Extender #(.in_width(5), .out_width(4), .\type ("zero")) bit_extender_1 (.in(cmd[11:7]), .out(rd));
  Bit_Extender #(.in_width(5), .out_width(4), .\type ("zero")) bit_extender_2 (.in(cmd[19:15]), .out(rs1));
  assign imm = {{20{cmd[31]}}, cmd[31:20]};  // Bit_Extender bit_extender_3
endmodule

module decode_S (
  input  [31:0] cmd,
  output [3:0] rs1,
  output [3:0] rs2,
  output [31:0] imm
);

  Bit_Extender #(.in_width(5), .out_width(4), .\type ("zero")) bit_extender_1 (.in(cmd[19:15]), .out(rs1));
  Bit_Extender #(.in_width(5), .out_width(4), .\type ("zero")) bit_extender_2 (.in(cmd[24:20]), .out(rs2));
  assign imm = {{20{cmd[31]}}, {cmd[31:25], cmd[11:7]}};  // Bit_Extender bit_extender_3
endmodule

module encoder_42 (
  input  A0,
  input  A1,
  input  A2,
  input  A3,
  output [1:0] Y
);

  or or_1 (Y[0], A1, A3);
  or or_2 (Y[1], A2, A3);
endmodule

module encoder_83 (
  input  A0,
  input  A1,
  input  A2,
  input  A3,
  input  A4,
  input  A5,
  input  A6,
  input  A7,
  output [2:0] Y
);

  wire [1:0] encoder_42_1_y, encoder_42_2_y;

  or or_1 (Y[2], A4, A5, A6, A7);
  encoder_42 encoder_42_1 (.A0(A0), .A1(A1), .A2(A2), .A3(A3), .Y(encoder_42_1_y));
  encoder_42 encoder_42_2 (.A0(A4), .A1(A5), .A2(A6), .A3(A7), .Y(encoder_42_2_y));
  Multiplexer #(.width(2)) multiplexer_1 (.in0(encoder_42_1_y), .in1(encoder_42_2_y), .out(Y[1:0]), .sel(Y[2]));
endmodule

module decoder_IO (
  input  [31:0] in_1,
  output isVGA,
  output isMem
);

  wire comparator_1_eq, comparator_1_gt, comparator_2_lt, or_1_out;

  Comparator #(.width(32)) comparator_1 (
    .a(in_1), .b(32'h20000000), .gt(comparator_1_gt), .eq(comparator_1_eq));  // open: lt
  Comparator #(.width(32)) comparator_2 (.a(in_1), .b(32'h20040000), .lt(comparator_2_lt));  // open: gt, eq
  or or_1 (or_1_out, comparator_1_gt, comparator_1_eq);
  and and_1 (isVGA, or_1_out, comparator_2_lt);
  not not_1 (isMem, isVGA);
endmodule
